// Logisim project ppi2.circ as structural Verilog: 1 circuit, main circuit main
module main (
  input  A,
  input  B,
  input  C,
  input  D,
  output A_D,
  output B_D,
  output C_D,
  output D_D,
  output A_K,
  output B_K,
  output C_K,
  output D_K
);

  wire a_b_c_d_out, a_b_c_out, a_b_nc_nd_out, a_b_out, a_c_nd_out, a_nb_c_d_out, a_nb_c_nd_out,
       a_nb_nc_d_out, a_nb_nc_out, a_nd_out, b_nc_nd_out, bc_out, bd_out, nA_2_out, na_nb_nc_nd_out, nA_out,
       nabcd_out, nB_2_out, nb_ncd_out, nB_out, nbc_nd_out, nbc_out, nC_2_out, nC_out, nD_2_out, nD_out;

  nand nA (nA_out, A, A);
  nand nB (nB_out, B, B);
  nor nB_2 (nB_2_out, B, B);
  nor nA_2 (nA_2_out, A, A);
  nand nC (nC_out, C, C);
  nor nC_2 (nC_2_out, C, C);
  nand nD (nD_out, D, D);
  nor nD_2 (nD_2_out, D, D);
  nand a_nd (a_nd_out, A, nD_out);
  nand bd (bd_out, B, D);
  nand b_nc_nd (b_nc_nd_out, B, nC_out, nD_out);
  nand bc (bc_out, B, C);
  nand nbc (nbc_out, nB_out, C);
  nand nabcd (nabcd_out, nA_out, B, C, D);
  nand nb_ncd (nb_ncd_out, nB_out, nC_out, D);
  nand nbc_nd (nbc_nd_out, nB_out, C, nD_out);
  nor a_b (a_b_out, A, B);
  nor a_nb_nc_d (a_nb_nc_d_out, A, nB_2_out, nC_2_out, D);
  nor a_nb_c_d (a_nb_c_d_out, A, nB_2_out, C, D);
  nor a_b_c (a_b_c_out, A, B, C);
  nor a_c_nd (a_c_nd_out, A, C, nD_2_out);
  nor a_nb_nc (a_nb_nc_out, A, nB_2_out, nC_2_out);
  nor a_b_c_d (a_b_c_d_out, A, B, C, D);
  nor a_b_nc_nd (a_b_nc_nd_out, A, B, nC_2_out, nD_2_out);
  nor a_nb_c_nd (a_nb_c_nd_out, A, nB_2_out, C, nD_2_out);
  nor na_nb_nc_nd (na_nb_nc_nd_out, nA_2_out, nB_2_out, nC_2_out, nD_2_out);
  nand a_nd_bd_b_nc_nd (A_D, a_nd_out, bd_out, b_nc_nd_out);
  nand bd_bc (B_D, bd_out, bc_out);
  nand nbc_b_nc_nd_na (C_D, b_nc_nd_out, nbc_out, nA_out);
  nand abcd_nb_ncd_nbc_nd_b_nc_nd_a_nd (D_D, nabcd_out, nb_ncd_out, nbc_nd_out, b_nc_nd_out, a_nd_out);
  nor a_b___a_nb_nc_d (A_K, a_b_out, a_nb_nc_d_out);
  nor a_b___a_nb_c_d (B_K, a_nb_c_d_out, a_b_out);
  nor a_b_c___a_c_nd___a_nc_d (C_K, a_b_c_out, a_c_nd_out, a_nb_nc_out);
  nor a_b_c_d___a_b_nc_nd___a_nb_c_nd___a_nb_nc_d___na_nb_nc_nd (D_K, a_nb_nc_d_out, a_b_c_d_out, a_b_nc_nd_out, a_nb_c_nd_out, na_nb_nc_nd_out);
endmodule
