// Logisim project PPI_2_MeravyMurarik.circ as structural Verilog: 1 circuit, main circuit main
module main (
  input  A,
  input  B,
  input  C,
  input  D,
  output P1,
  output P2,
  output P3,
  output P4,
  output P1_2,
  output P1_3,
  output P1_4,
  output P1_5
);

  wire A_nB_nD_out, ACD_out, B_nD_out, BC_out, BD_out, n_A_nC_out, n_B_D_out, n_C_nD_out, n_nA_C_out,
       n_nC_D_out, nA_B_out, nA_nD_out, nACD_out, nand_1_out, nand_2_out, nand_3_out, nand_4_out, nB_nC_out,
       nC_nD_out, nor_1_out, nor_2_out, nor_3_out, nor_4_out;

  nand nand_1 (nand_1_out, B, B);
  nand nand_2 (nand_2_out, A, A);
  nor nor_1 (nor_1_out, B, B);
  nor nor_2 (nor_2_out, A, A);
  nand nand_3 (nand_3_out, C, C);
  nor nor_3 (nor_3_out, C, C);
  nand nand_4 (nand_4_out, D, D);
  nor nor_4 (nor_4_out, D, D);
  nand nACD (nACD_out, nand_2_out, C, D, D);
  nand BC (BC_out, B, C);
  nand nB_nC (nB_nC_out, nand_1_out, nand_3_out);
  nand BD (BD_out, B, D);
  nand nA_nD (nA_nD_out, nand_2_out, nand_4_out);
  nand nC_nD (nC_nD_out, nand_3_out, nand_4_out);
  nand ACD (ACD_out, A, C, C, D);
  nand A_nB_nD (A_nB_nD_out, A, nand_1_out, nand_4_out);
  nor nA_B (nA_B_out, nor_2_out, B);
  nor n_C_nD (n_C_nD_out, C, nor_4_out);
  nor n_nC_D (n_nC_D_out, nor_3_out, D);
  nor n_nA_C (n_nA_C_out, nor_2_out, C);
  nor n_A_nC (n_A_nC_out, A, nor_3_out);
  nor n_B_D (n_B_D_out, nor_1_out, D);
  nor B_nD (B_nD_out, B, nor_4_out);
  nor n_nA_B (P1_2, nA_B_out, nA_B_out);
  nor nor_5 (P1_3, n_C_nD_out, n_nC_D_out);
  nor nor_6 (P1_4, n_nA_C_out, n_A_nC_out);
  nor nor_7 (P1_5, n_B_D_out, B_nD_out);
  nand nand_5 (P1, nACD_out, BC_out, nB_nC_out, BD_out, nA_nD_out, nC_nD_out);
  nand nand_6 (P2, nACD_out, ACD_out, nC_nD_out);
  nand nand_7 (P3, nB_nC_out, BC_out, A_nB_nD_out, ACD_out);
  nand nand_8 (P4, A_nB_nD_out, BD_out, nA_nD_out);

  // Notes on the sheet:
  //   MDNF
  //   MKNF
endmodule
