// Logisim project 3_zad_new.circ as structural Verilog: 1 circuit, main circuit main
module main (
  input  X,
  input  Res,
  output Y
);

  wire CLK_out, J1_out, J2_out, J3_out, j_k_ff_1_q, j_k_ff_1_qn, j_k_ff_2_q, j_k_ff_2_qn, j_k_ff_3_q,
       j_k_ff_3_qn, K1_out, K2_out, K3_out, nand_1_out, nX_nZ2_out, nX_Z1_Z3_out, nX_Z2_out, nZ1_Z3_out,
       X_nZ2_out, X_Z2_nZ3_out, X_Z2_Z3_out, X_Z3_out, Z1_Z2_Z3_out;

  nand nand_1 (nand_1_out, X, X);
  Clock CLK (.out(CLK_out));
  nand X_Z2_Z3 (X_Z2_Z3_out, j_k_ff_2_q, j_k_ff_3_q, X);
  nand nX_nZ2 (nX_nZ2_out, nand_1_out, j_k_ff_2_qn);
  nand X_Z2_nZ3 (X_Z2_nZ3_out, X, j_k_ff_2_q, j_k_ff_3_qn);
  nand nX_Z1_Z3 (nX_Z1_Z3_out, nand_1_out, j_k_ff_1_q, j_k_ff_3_q);
  nand X_Z3 (X_Z3_out, X, j_k_ff_3_q);
  nand nZ1_Z3 (nZ1_Z3_out, j_k_ff_1_qn, j_k_ff_1_qn, j_k_ff_3_q);
  nand X_nZ2 (X_nZ2_out, X, j_k_ff_2_qn);
  nand nX_Z2 (nX_Z2_out, nand_1_out, nand_1_out, j_k_ff_2_q);
  nand Z1_Z2_Z3 (Z1_Z2_Z3_out, j_k_ff_1_q, j_k_ff_2_q, j_k_ff_3_q);
  nand nand_2 (Y, Z1_Z2_Z3_out, Z1_Z2_Z3_out);
  nand J1 (J1_out, X_Z2_Z3_out, X_Z2_Z3_out);
  nand K1 (K1_out, nX_nZ2_out, X_Z2_nZ3_out, nX_Z1_Z3_out);
  nand J2 (J2_out, nX_Z1_Z3_out, X_Z3_out);
  nand K2 (K2_out, X_Z3_out, nZ1_Z3_out, nX_Z1_Z3_out);
  nand J3 (J3_out, X_nZ2_out, nX_Z2_out);
  nand K3 (K3_out, nZ1_Z3_out, X_Z3_out, nX_Z2_out);
  J_K_Flip_Flop j_k_ff_1 (
    .J(J1_out), .clk(CLK_out), .K(K1_out), .Q(j_k_ff_1_q), .Qn(j_k_ff_1_qn), .reset(Res));  // open: preset, en
  J_K_Flip_Flop j_k_ff_2 (
    .J(J2_out), .clk(CLK_out), .K(K2_out), .Q(j_k_ff_2_q), .Qn(j_k_ff_2_qn), .reset(Res));  // open: preset, en
  J_K_Flip_Flop j_k_ff_3 (
    .J(J3_out), .clk(CLK_out), .K(K3_out), .Q(j_k_ff_3_q), .Qn(j_k_ff_3_qn), .reset(Res));  // open: preset, en
endmodule
