// Logisim project 3_zad.circ as structural Verilog: 1 circuit, main circuit main
module main (
  input  X,
  input  Res,
  output Y
);

  wire CLK_out, nand_1_out, nx_nz1_z2_out, nx_nz1_z2_z1_nz2_x_nz2_out, nX_out, nx_z1_z2_nx_z3_x_nz3_out,
       nx_z1_z2_out, nx_z2_z3_out, nx_z2_z3_x_z1_z2_x_z3_out, nx_z3_out, nx_z3_z2_2_out, nx_z3_z2_out,
       x_nz2_nx_z3_out, x_nz2_out, x_nz3_out, x_z1_z2_out, x_z3_2_out, x_z3_out, z1_nz2_out, Z1_q, Z1_qn,
       Z2_q, Z2_qn, Z3_q, Z3_qn;

  nand nX (nX_out, X, X);
  Clock CLK (.out(CLK_out));
  nand nand_1 (nand_1_out, X, Z1_q, Z2_q);
  nand nx_z3_z2 (nx_z3_z2_out, Z2_q, Z3_q, nX_out);
  nand nx_z1_z2 (nx_z1_z2_out, nX_out, Z1_q, Z2_q);
  nand nx_z3 (nx_z3_out, nX_out, Z3_q);
  nand x_z3 (x_z3_out, X, Z3_q);
  nand nx_z2_z3 (nx_z2_z3_out, nX_out, Z2_q, Z3_q);
  nand x_z1_z2 (x_z1_z2_out, X, Z1_q, Z2_q);
  nand nx_nz1_z2 (nx_nz1_z2_out, nX_out, Z1_qn, Z2_q);
  nand z1_nz2 (z1_nz2_out, Z1_q, Z2_qn);
  nand x_nz2 (x_nz2_out, X, Z2_qn);
  nand x_nz3 (x_nz3_out, X, Z3_qn);
  nand nand_2 (Y, nand_1_out, nand_1_out);
  nand nx_z3_z2_2 (nx_z3_z2_2_out, nx_z3_z2_out, nx_z3_z2_out);
  nand nx_z1_z2_nx_z3_x_nz3 (nx_z1_z2_nx_z3_x_nz3_out, nx_z1_z2_out, nx_z3_out, x_nz3_out);
  nand x_z3_2 (x_z3_2_out, x_z3_out, x_z3_out);
  nand nx_z2_z3_x_z1_z2_x_z3 (nx_z2_z3_x_z1_z2_x_z3_out, nx_z2_z3_out, x_z3_out, x_z1_z2_out);
  nand nx_nz1_z2_z1_nz2_x_nz2 (nx_nz1_z2_z1_nz2_x_nz2_out, nx_nz1_z2_out, z1_nz2_out, x_nz2_out);
  nand x_nz2_nx_z3 (x_nz2_nx_z3_out, nx_z3_out, x_nz2_out);
  J_K_Flip_Flop Z1 (
    .J(nx_z3_z2_2_out), .clk(CLK_out), .K(nx_z1_z2_nx_z3_x_nz3_out), .Q(Z1_q), .Qn(Z1_qn), .reset(Res));  // open: preset, en
  J_K_Flip_Flop Z2 (
    .J(x_z3_2_out), .clk(CLK_out), .K(nx_z2_z3_x_z1_z2_x_z3_out), .Q(Z2_q), .Qn(Z2_qn), .reset(Res));  // open: preset, en
  J_K_Flip_Flop Z3 (
    .J(nx_nz1_z2_z1_nz2_x_nz2_out), .clk(CLK_out), .K(x_nz2_nx_z3_out), .Q(Z3_q), .Qn(Z3_qn), .reset(Res));  // open: preset, en
endmodule
